# Fritzing sketch ACS712_AmMeter_Test1 (saved by Fritzing 0.9.4)
breadboards: 1

parts:
  パーツ1 = Arduino Pro Mini (5V)  # not connected
  IC1 = IC, DIP package, 16 pins [chip_label=MCP3208]
  C1 = Ceramic Capacitor [capacitance=100nF package="100 mil [THT, multilayer]"]
  C2 = Electrolytic Capacitor [capacitance=1µF package="100 mil [THT, electrolytic]"]

nets:
  N1: IC1.pin3, IC1.pin4, IC1.pin5, IC1.pin6, IC1.pin7, IC1.pin8, IC1.pin12, IC1.pin14, C2.-
  N2: IC1.pin15, IC1.pin16, C1.1, C2.+

notes:
  AGND
  +5V
  DGND
  +5V
  MCP3208
  1 CH0 14 VDD
  2 CH1 13 VREF
  3 CH2 12 AGND
  4 CH3 11 CLK
  5 CH4 10 DOUT
  6 CH5 9 DIN
  7 CH7 8 !CS/SHDN
