# Fritzing sketch ACS712_AmMeter_Test2 (saved by Fritzing 0.9.3b)
breadboards: 2
perfboards: 2

parts:
  パーツ1 = Arduino Pro Mini (5V)
  U2 = mystery part, 4 pins [chip_label=NJM2396]
  C1 = Ceramic Capacitor [capacitance=100nF package="100 mil [THT, multilayer]"]
  C2 = Ceramic Capacitor [capacitance=100nF package="100 mil [THT, multilayer]"]
  C3 = Electrolytic Capacitor [capacitance=1µF package="100 mil [THT, electrolytic]"]
  C4 = Electrolytic Capacitor [capacitance=1µF package="100 mil [THT, electrolytic]"]
  R1 = Resistor [tolerance=±5% resistance=1k package=THT]
  R2 = Resistor [tolerance=±5% resistance=1k package=THT]
  U1 = mystery part, 4 pins [chip_label="SSD1306 I2C"]
  R3 = Resistor [tolerance=±5% resistance=100k package=THT]
  R4 = Resistor [tolerance=±5% resistance=100k package=THT]
  VCC1 = Battery
  C5 = Electrolytic Capacitor [capacitance=1µF package="100 mil [THT, electrolytic]"]
  D1 = Rectifier Diode [part_number=1N4001 package="300 mil [THT]"]

nets:
  N1: パーツ1.A4, R2.Pin_0, U1.pin1
  N2: パーツ1.A5, R1.Pin_0, U1.pin2
  N3: U2.pin1, C1.1, R3.Pin_0, VCC1.+, C5.+, D1.cathode
  N4: U2.pin2, C2.0, C3.+, C4.+, R1.Pin_1, R2.Pin_1, U1.pin3, D1.anode
  N5: U2.pin3, C1.0, C2.1, C3.-, C4.-, U1.pin4, R4.Pin_0, VCC1.-, C5.-
  N6: R3.Pin_1, R4.Pin_1

notes:
  SSD1306 I2C
  1 GND
  2 VCC
  3 SCL
  4 SDA
  GND+6V
  GND+5V
  DGND
  +5V
  NJM2396
  1 VIN
  2 VOUT
  3 GND
  4 ON/OFF
  6V
  AAA x 4
  AGND
  +5V
