# Fritzing sketch ACS712_AmMeter_Test3 (saved by Fritzing 0.9.3b)
breadboards: 2

parts:
  U2 = mystery part, 4 pins [chip_label=NJM2396]
  C1 = Ceramic Capacitor [capacitance=100nF package="100 mil [THT, multilayer]"]
  C2 = Ceramic Capacitor [capacitance=100nF package="100 mil [THT, multilayer]"]
  C3 = Electrolytic Capacitor [capacitance=1µF package="100 mil [THT, electrolytic]"]
  VCC1 = Battery
  C5 = Electrolytic Capacitor [capacitance=1µF package="100 mil [THT, electrolytic]"]
  D1 = Rectifier Diode [part_number=1N4001 package="300 mil [THT]"]
  IC1 = IC, DIP package, 8 pins [chip_label=" NJU7032"]
  U3 = mystery part, 3 pins [chip_label=2426]
  C6 = Electrolytic Capacitor [capacitance=1µF package="100 mil [THT, electrolytic]"]
  C7 = Electrolytic Capacitor [capacitance=1µF package="100 mil [THT, electrolytic]"]

nets:
  N1: U2.pin1, C1.1, VCC1.+, C5.+, D1.cathode
  N2: U2.pin2, C2.0, C3.+, D1.anode, IC1.pin8, U3.pin3, C6.+
  N3: U2.pin3, C1.0, C2.1, C3.-, VCC1.-, C5.-, IC1.pin4, U3.pin2, C7.-
  N4: IC1.pin5, U3.pin1, C6.-, C7.+
  N5: IC1.pin6, IC1.pin7

notes:
  GND+6V
  NJM2396
  1 VIN
  2 VOUT
  3 GND
  4 ON/OFF
  6V
  AAA x 4
  GND+5V
  2.5V +5V
  GND
  +2.5V
