# Fritzing sketch ACS712_AmMeter_VCVS_LPF (saved by Fritzing 0.9.3b)
breadboards: 1
perfboards: 1

parts:
  IC1 = IC, DIP package, 8 pins [chip_label=" NJU7032"]
  U3 = mystery part, 3 pins [chip_label=2426]
  C6 = Electrolytic Capacitor [capacitance=1µF package="100 mil [THT, electrolytic]"]
  C7 = Electrolytic Capacitor [capacitance=1µF package="100 mil [THT, electrolytic]"]
  C8 = Ceramic Capacitor [capacitance=100nF package="100 mil [THT, multilayer]"]
  C9 = Ceramic Capacitor [capacitance=100nF package="100 mil [THT, multilayer]"]
  R1 = Resistor [tolerance=±5% resistance=15k package=THT]
  R2 = Resistor [tolerance=±5% resistance=15k package=THT]
  C10 = Ceramic Capacitor [capacitance=100nF package="100 mil [THT, multilayer]"]
  C11 = Ceramic Capacitor [capacitance=100nF package="100 mil [THT, multilayer]"]

nets:
  N1: IC1.pin1, IC1.pin2, C10.0
  N2: IC1.pin3, C8.0, R1.Pin_0
  N3: IC1.pin4, U3.pin2, C7.-, C9.0
  N4: IC1.pin5, U3.pin1, C6.-, C7.+, C8.1, C9.1, C11.0
  N5: IC1.pin6, IC1.pin7
  N6: IC1.pin8, U3.pin3, C6.+, C11.1
  N7: R1.Pin_1, R2.Pin_0, C10.1

notes:
  2.5V +5V
  GND
  +2.5V
  OUT
  ACS712 Module
